# Fritzing sketch test_breadboard (saved by Fritzing 0.9.6b)
breadboards: 2

parts:
  U1 = LuaNode32 / ESP32 [part_number=ESP32S-PIN30]
  Servo_J1 = Dagu DGServo 9g header (male) [package=THT]
  Servo_J2 = Dagu DGServo 9g header (male) [package=THT]
  HC-SR04_Sensor_1 = HC-SR04 Ultrasonic Distance Sensor
  R1 = Resistor [tolerance=±5% power=0.25 resistance=1.8k package=THT]
  R2 = Resistor [tolerance=±5% power=0.25 resistance=3.3k package=THT]

nets:
  N1: U1.D32, Servo_J1.pulse
  N2: U1.D33, Servo_J2.pulse
  N3: U1.D12, HC-SR04_Sensor_1.TRIG
  N4: U1.D13, R1.Pin_1, R2.Pin_0
  GND: U1.GND, Servo_J1.gnd, Servo_J2.gnd, HC-SR04_Sensor_1.GND, R2.Pin_1
  5V: U1.Vin, Servo_J1.Vcc, Servo_J2.Vcc, HC-SR04_Sensor_1.VCC
  N5: HC-SR04_Sensor_1.ECHO, R1.Pin_0

custom parts:
  LuaNode32 / ESP32: New Image for LuaNode32 DOIT ESP32 DEVKIT V1. Base parts from LuaNode32 / ESP32 ESP32 based LuaNode32 by G.Noorlander DOIT Esp32 DevKit v1 (30 pins long, 11 pins width) by Werner Rothschopf (modified by vanepp Dec 2018)
